# Fritzing sketch HardwarSerial (saved by Fritzing 0.9.1b)
breadboards: 1

parts:
  U1 = HC-05 Bluetooth Transceiver Breakout Board, 5V, 6pin [chip_label=IC package=SIP]
  Arduino1 = Arduino Uno (Rev3)

nets:
  N1: U1.Key, Arduino1.D3_PWM
  VCC: U1.VCC, Arduino1.5V
  GND: U1.GND, Arduino1.GND
  N2: U1.RX, Arduino1.D0/RX
  N3: U1.TX, Arduino1.D1/TX
  N4: U1.STATE, Arduino1.D2

custom parts:
  HC-05 Bluetooth Transceiver Breakout Board, 5V, 6pin: Breakout board for HC-05 with 5V-to-3V translation, command mode pin (KEY) and STATE pin. http://www.ebay.com/itm/HC-05-Bluetooth-Transceiver-Host-Slave-Master-Module-Wireless-Serial-6pin-/221158958927?pt=LH_DefaultDomain_0&hash=item337e19e74f
