# Fritzing sketch ImprovedPowerCtrl (saved by Fritzing 0.9.1b)
breadboards: 1

parts:
  Arduino1 = Arduino Uno (Rev3)
  Q1 = PNP-Transistor [part_number=2N2907 package="TO92 [THT]"]
  Q2 = NPN-Transistor [part_number=2N2222 package="TO92 [THT]"]
  R1 = Resistor [tolerance=±5% resistance=1k package=THT]
  R2 = Resistor [tolerance=±5% resistance=1k package=THT]
  U1 = HC-05 Bluetooth Transceiver Breakout Board, 5V, 6pin [package=SIP]

nets:
  N1: Arduino1.A2, U1.Key
  N2: Arduino1.A3, U1.RX
  N3: Arduino1.A4/SDA, U1.TX
  N4: Arduino1.A5/SCL, U1.STATE
  N5: Arduino1.D7, R2.Pin_0
  N6: Arduino1.5V, Q1.C, R1.Pin_1
  GND: Arduino1.GND, Q2.E, U1.GND
  N7: Q1.E, U1.VCC
  N8: Q1.B, Q2.C, R1.Pin_0
  N9: Q2.B, R2.Pin_1

custom parts:
  HC-05 Bluetooth Transceiver Breakout Board, 5V, 6pin: Breakout board for HC-05 with 5V-to-3V translation, command mode pin (KEY) and STATE pin. http://www.ebay.com/itm/HC-05-Bluetooth-Transceiver-Host-Slave-Master-Module-Wireless-Serial-6pin-/221158958927?pt=LH_DefaultDomain_0&hash=item337e19e74f
